// Logisim project circuit.circ as structural Verilog: 1 circuit, main circuit main
module main (
  input  [3:0] in_1,
  input  in_2,
  input  in_3,
  input  [3:0] in_4,
  input  in_5,
  input  in_6,
  input  in_7,
  input  [3:0] in_8,
  input  in_9,
  output [3:0] out_10
);

  wire button_1_out, button_2_out, button_3_out, clock_1_out, clock_2_out, clock_3_out, comparator_1_eq,
       comparator_2_eq, comparator_3_eq, demultiplexer_1_out0, demultiplexer_1_out1, demultiplexer_1_out2,
       demultiplexer_1_out3, not_1_out, not_2_out, not_3_out, not_4_out;
  wire [1:0] counter_3_q;
  wire [3:0] controlled_buffer_1_out, controlled_buffer_2_out, controlled_buffer_3_out, counter_2_q,
       multiplexer_1_out, multiplexer_2_out, pull_resistor_3_node, ram_1_data, ram_2_data, ram_3_data,
       ram_4_data, ram_5_data, register_1_q, register_2_q, register_3_q, register_4_q;
  wire [3:2] counter_3_q_2;

  Clock clock_1 (.out(clock_1_out));
  Button button_1 (.out(button_1_out));
  Clock clock_2 (.out(clock_2_out));
  Button button_2 (.out(button_2_out));
  LED led_1 (.in(comparator_1_eq));
  not not_1 (not_1_out, comparator_1_eq);
  LED led_2 (.in(not_1_out));
  Counter #(.width(4), .max('hf)) counter_1 (
    .Q(out_10), .clk(clock_1_out), .clr(button_1_out));  // open: load, D, count, carry
  LED led_3 (.in(comparator_2_eq));
  not not_2 (not_2_out, comparator_2_eq);
  LED led_4 (.in(not_2_out));
  Counter #(.width(4), .max('hf)) counter_2 (
    .Q(counter_2_q), .clk(clock_2_out), .clr(button_2_out));  // open: load, D, count, carry
  // Probe on counter_2_q
  RAM #(.addrWidth(4), .dataWidth(4)) ram_1 (
    .addr(out_10), .data(ram_1_data), .sel(in_2), .clk(clock_1_out), .ld(in_3), .clr(in_5));
  // Probe on ram_1_data
  Pull_Resistor pull_resistor_1 (.node(ram_1_data));
  RAM #(.addrWidth(2), .dataWidth(4)) ram_2 (
    .addr(counter_2_q[1:0]), .data(ram_2_data), .sel(in_6), .clk(clock_2_out), .ld(in_7), .clr(in_9));
  Pull_Resistor pull_resistor_2 (.node(ram_2_data));
  // Probe on ram_2_data
  Multiplexer #(.width(4)) multiplexer_1 (
    .in0(ram_1_data), .in1(ram_3_data), .out(multiplexer_1_out), .sel(comparator_1_eq));  // open: en
  // Probe on multiplexer_1_out
  assign controlled_buffer_1_out = comparator_1_eq ? out_10 : 4'bz;  // Controlled_Buffer controlled_buffer_1
  Multiplexer #(.width(4)) multiplexer_2 (
    .in0(ram_2_data), .in1(ram_4_data), .out(multiplexer_2_out), .sel(comparator_2_eq));  // open: en
  // Probe on multiplexer_2_out
  assign controlled_buffer_2_out = comparator_2_eq ? counter_2_q : 4'bz;  // Controlled_Buffer controlled_buffer_2
  Comparator #(.width(4)) comparator_1 (.a(ram_1_data), .b(in_4), .eq(comparator_1_eq));  // open: gt, lt
  Comparator #(.width(4)) comparator_2 (.a(ram_2_data), .b(in_8), .eq(comparator_2_eq));  // open: gt, lt
  // Probe on controlled_buffer_1_out
  // Probe on controlled_buffer_2_out
  LED led_5 (.in(comparator_2_eq));
  RAM #(.addrWidth(4), .dataWidth(4)) ram_3 (
    .addr(controlled_buffer_1_out), .data(ram_3_data), .sel(comparator_1_eq), .clk(clock_1_out),
    .ld(comparator_1_eq));  // open: clr
  RAM #(.addrWidth(4), .dataWidth(4)) ram_4 (
    .addr(controlled_buffer_2_out), .data(ram_4_data), .sel(comparator_2_eq), .clk(clock_2_out),
    .ld(comparator_2_eq));  // open: clr
  // Probe on ram_3_data
  // Probe on ram_4_data
  Button button_3 (.out(button_3_out));
  Clock clock_3 (.out(clock_3_out));
  not not_3 (not_3_out, clock_3_out);
  LED led_6 (.in(comparator_3_eq));
  not not_4 (not_4_out, comparator_3_eq);
  LED led_7 (.in(not_4_out));
  Counter #(.width(4), .max('hf)) counter_3 (
    .Q({counter_3_q_2, counter_3_q}), .clk(clock_3_out), .clr(button_3_out));  // open: load, D, count, carry
  // Probe on {counter_3_q_2, counter_3_q}
  Demultiplexer #(.select(2)) demultiplexer_1 (
    .out0(demultiplexer_1_out0), .out1(demultiplexer_1_out1), .out2(demultiplexer_1_out2),
    .out3(demultiplexer_1_out3), .in(not_3_out), .sel(counter_3_q));  // open: en
  Register #(.width(4)) register_1 (
    .D(ram_5_data), .Q(register_1_q), .clk(demultiplexer_1_out0), .clr(button_3_out));  // open: en
  Register #(.width(4)) register_2 (
    .D(ram_5_data), .Q(register_2_q), .clk(demultiplexer_1_out1), .clr(button_3_out));  // open: en
  Register #(.width(4)) register_3 (
    .D(ram_5_data), .Q(register_3_q), .clk(demultiplexer_1_out2), .clr(button_3_out));  // open: en
  Register #(.width(4)) register_4 (
    .D(ram_5_data), .Q(register_4_q), .clk(demultiplexer_1_out3), .clr(button_3_out));  // open: en
  Pull_Resistor pull_resistor_3 (.node(pull_resistor_3_node));
  Multiplexer #(.select(2), .width(4)) multiplexer_3 (
    .in0(register_1_q), .in1(register_2_q), .in2(register_3_q), .in3(register_4_q),
    .out(pull_resistor_3_node), .sel(counter_3_q));  // open: en
  assign controlled_buffer_3_out = comparator_3_eq ? {counter_3_q_2, counter_3_q} : 4'bz;  // Controlled_Buffer controlled_buffer_3
  // Probe on pull_resistor_3_node
  Comparator #(.width(4)) comparator_3 (.a(in_1), .b(pull_resistor_3_node), .eq(comparator_3_eq));  // open: gt, lt
  // Probe on controlled_buffer_3_out
  LED led_8 (.in(comparator_3_eq));
  // Probe on ram_5_data
  RAM #(.addrWidth(4), .dataWidth(4)) ram_5 (
    .addr(controlled_buffer_3_out), .data(ram_5_data), .sel(comparator_3_eq), .clk(clock_3_out),
    .ld(comparator_3_eq));  // open: clr

  // Notes on the sheet:
  //   Main Memory
  //   Cache Memory
  //   Main Memory
  //   Cache Memory
  //   Cache Memory
  //   Cache Memory Basic Circuit
  //   If counter value in cache then cache 'HIT' and output given from cache
  //   else it searches for the value of counter in main memory
  //   Direct Mapping in Cache
  //   NOTE : When HIT occurs in cache memory, the Main Memory will be free and can be utilized simultaneously for other operations (for eg. I/O, etc.)
  //   OUTPUT
  //   COMPARATOR
  //   COMPARATOR
  //   Main Memory
  //   Free ?
  //   Main Memory
  //   Cache Memory
  //   Direct Mapping with Cache Memory Filling
  //   COMPARATOR
  //   OUTPUT
  //   Free ?
endmodule
